// Logisim project Destination.circ as structural Verilog: 1 circuit, main circuit main
module main (
  input  Temperature,
  input  Radiation,
  input  Oxygen,
  input  Life,
  input  [9:0] in_5,
  input  [9:0] in_6,
  input  in_7,
  output [1:0] out_8,
  output [9:0] out_9
);

  wire and_1_out, comparator_1_eq, comparator_1_lt, comparator_2_lt, not_1_out, or_1_out, or_2_out;
  wire [0:0] comparator_1_gt;

  Comparator #(.width(10), .mode("unsigned")) comparator_1 (
    .a(in_5), .b(in_6), .gt(comparator_1_gt[0]), .eq(comparator_1_eq), .lt(comparator_1_lt));
  or or_1 (or_1_out, comparator_1_eq, comparator_1_lt);
  not not_1 (not_1_out, Radiation);
  Shifter #(.width(10), .shift("lr")) shifter_1 (.in(in_5), .\dist ({{3{in_7}}, comparator_1_gt[0]}), .out(out_9));
  and and_1 (and_1_out, Temperature, not_1_out, Oxygen, Life);
  Comparator #(.width(10), .mode("unsigned")) comparator_2 (.a(out_9), .b(in_6), .lt(comparator_2_lt));  // open: gt, eq
  or or_2 (or_2_out, comparator_2_lt, or_1_out);
  not not_2 (out_8[0], and_1_out);
  not not_3 (out_8[1], or_2_out);

  // Notes on the sheet:
  //   Altitude check
  //   Habitability (ERR)
endmodule
